// Digital circuit 1bit-Compar.dig as structural Verilog
module _1bit_Compar (
  input  _1_eq,
  input  A,
  input  B,
  output eq,
  output gt,
  output lt
);

  wire and_1_out, and_2_out, not_1_out, not_2_out;

  not not_1 (not_1_out, A);
  not not_2 (not_2_out, B);
  and and_1 (and_1_out, _1_eq, not_1_out, not_2_out);
  and and_2 (and_2_out, _1_eq, A, B);
  and and_3 (gt, _1_eq, A, not_2_out);
  and and_4 (lt, _1_eq, not_1_out, B);
  or or_1 (eq, and_1_out, and_2_out);
endmodule
