// Digital circuit 4 bit - opposite.dig as structural Verilog
module _4_bit___opposite (
  input  [3:0] Num,
  input  Cin,
  output [3:0] Output
);

  wire _4bit_fa_1_ov;
  wire [3:0] _4bit___checker_1_out, not_1_out;

  _4bit___Checker _4bit___checker_1 (.Num(Num), .Cin(Cin), .Out(_4bit___checker_1_out));
  assign not_1_out = ~_4bit___checker_1_out;  // Not not_1, 4 bits wide
  _4bit_Fa _4bit_fa_1 (.A(not_1_out), .B(4'b0000), .Cin(1'b1), .S(Output), .Ov(_4bit_fa_1_ov));
  LED led_1 (.in(_4bit_fa_1_ov));
endmodule
