// Digital circuit 4 bit -Compair.dig as structural Verilog
module _4_bit__Compair (
  input  [3:0] A,
  input  [3:0] B,
  output eq,
  output gt,
  output lt
);

  wire _1_eq_1, _1_eq_2, _1_eq_3, _1bit_compar_1_gt, _1bit_compar_1_lt, _1bit_compar_2_gt, _1bit_compar_2_lt,
       _1bit_compar_3_gt, _1bit_compar_3_lt, _1bit_compar_4_gt, _1bit_compar_4_lt;

  _1bit_Compar _1bit_compar_1 (
    ._1_eq(1'b1), .A(A[3]), .B(B[3]), .eq(_1_eq_3), .gt(_1bit_compar_1_gt), .lt(_1bit_compar_1_lt));
  xor xor_1 (gt, _1bit_compar_4_gt, _1bit_compar_3_gt, _1bit_compar_2_gt, _1bit_compar_1_lt);
  _1bit_Compar _1bit_compar_2 (
    ._1_eq(_1_eq_3), .A(A[2]), .B(B[2]), .eq(_1_eq_2), .gt(_1bit_compar_2_gt), .lt(_1bit_compar_2_lt));
  _1bit_Compar _1bit_compar_3 (
    ._1_eq(_1_eq_2), .A(A[1]), .B(B[1]), .eq(_1_eq_1), .gt(_1bit_compar_3_gt), .lt(_1bit_compar_3_lt));
  _1bit_Compar _1bit_compar_4 (
    ._1_eq(_1_eq_1), .A(A[0]), .B(B[0]), .eq(eq), .gt(_1bit_compar_4_gt), .lt(_1bit_compar_4_lt));
  xor xor_2 (lt, _1bit_compar_4_lt, _1bit_compar_3_lt, _1bit_compar_2_lt, _1bit_compar_1_gt);
endmodule
