// Digital circuit 4bit - Checker.dig as structural Verilog
module _4bit___Checker (
  input  [3:0] Num,
  input  Cin,
  output [3:0] Out
);

  and and_1 (Out[3], Num[3], Cin);
  and and_2 (Out[2], Num[2], Cin);
  and and_3 (Out[1], Num[1], Cin);
  and and_4 (Out[0], Num[0], Cin);
endmodule
