// Digital circuit 4bit-Fa.dig as structural Verilog
module _4bit_Fa (
  input  [3:0] A,
  input  [3:0] B,
  input  Cin,
  output [3:0] S,
  output Ov
);

  wire fa_1_cout, fa_2_cout, fa_3_cout;

  Fa fa_1 (.A(A[0]), .B(B[0]), .Cin(Cin), .S(S[0]), .Cout(fa_1_cout));
  Fa fa_2 (.A(A[1]), .B(B[1]), .Cin(fa_1_cout), .S(S[1]), .Cout(fa_2_cout));
  Fa fa_3 (.A(A[2]), .B(B[2]), .Cin(fa_2_cout), .S(S[2]), .Cout(fa_3_cout));
  Fa fa_4 (.A(A[3]), .B(B[3]), .Cin(fa_3_cout), .S(S[3]), .Cout(Ov));
endmodule
