// Digital circuit 8 bit - oppposite raw.dig as structural Verilog
module _8_bit___oppposite_raw (
  input  [7:0] Num,
  output [7:0] Output
);

  wire _8bit_fa_1_ov;
  wire [7:0] not_1_out;

  assign not_1_out = ~Num;  // Not not_1, 8 bits wide
  _8bit_Fa _8bit_fa_1 (.A(not_1_out), .B({8{1'b0}}), .Cin(1'b1), .Ov(_8bit_fa_1_ov), .S(Output));
  LED led_1 (.in(_8bit_fa_1_ov));
endmodule
