// Digital circuit 8 bit ALU.dig as structural Verilog
module _8_bit_ALU (
  input  [7:0] A,
  input  [7:0] B,
  input  [2:0] Opcode,
  output [7:0] S,
  output Ov,
  output eq,
  output gt,
  output lt
);

  wire BitShift_Ov, Multi_Ov, or_1_out, Ov_4_bit_converter, Sub_ov, Sum_ov, xor_1_out, xor_2_out;
  wire [2:0] S___Comp;
  wire [7:0] S___BitShift, S___Multi, S___sub, S___sum;
  wire [7:3] multiplexer_2_out;

  Multiplexer #(.Bits(8), .Selector_Bits(3)) multiplexer_1 (
    .sel(Opcode), .in_0(S___sum), .in_1(S___sub), .in_2({8{1'b0}}), .in_3(S___BitShift), .in_4(S___Multi),
    .in_5({8{1'b0}}), .in_6({8{1'b0}}), .in_7({8{1'b0}}), .out(S));
  Multiplexer #(.Bits(8), .Selector_Bits(3)) multiplexer_2 (
    .sel(Opcode), .in_0({8{1'b0}}), .in_1({8{1'b0}}), .in_2({{5{1'b0}}, S___Comp}), .in_3({8{1'b0}}),
    .in_4({8{1'b0}}), .in_5({8{1'b0}}), .in_6({8{1'b0}}), .in_7({8{1'b0}}),
    .out({multiplexer_2_out, lt, gt, eq}));
  or or_1 (or_1_out, Multi_Ov, Ov_4_bit_converter);
  Multiplexer #(.Selector_Bits(3)) multiplexer_3 (
    .sel(Opcode), .in_0(Sum_ov), .in_1(Sub_ov), .in_2(1'b0), .in_3(1'b0), .in_4(or_1_out), .in_5(1'b0),
    .in_6(1'b0), .in_7(1'b0), .out(Ov));
  _8bit_Fa _8bit_fa_1 (.A(A), .B(B), .Cin(1'b0), .Ov(Sum_ov), .S(S___sum));
  _8bit_Fs _8bit_fs_1 (.A(A), .B(B), .S(S___sub), .Ov(Sub_ov));
  _8bit_Compar _8bit_compar_1 (.A(A), .B(B), .eq(S___Comp[0]), .gt(S___Comp[1]), .lt(S___Comp[2]));
  _8bit_bitshift _8bit_bitshift_1 (.In(A), .Drop(BitShift_Ov), .Out(S___BitShift));
  xor xor_1 (xor_1_out, A[4], A[5], A[6], A[7]);
  or or_2 (Ov_4_bit_converter, xor_1_out, xor_2_out);
  _8bit___int_Multiplier _8bit___int_multiplier_1 (.B(B[3:0]), .A(A[3:0]), .Output(S___Multi), .Ov(Multi_Ov));
  xor xor_2 (xor_2_out, B[7], B[6], B[5], B[4]);
endmodule
