// Digital circuit 8bit - int Multiplier.dig as structural Verilog
module _8bit___int_Multiplier (
  input  [3:0] B,
  input  [3:0] A,
  output [7:0] Output,
  output Ov
);

  wire _4_bit__compair_1_eq, _4_bit__compair_1_gt, _4_bit__compair_1_lt, _4_bit__compair_2_eq,
       _4_bit__compair_2_gt, _4_bit__compair_2_lt, _8bit_bitshift_1_drop, _8bit_bitshift_2_drop,
       _8bit_bitshift_3_drop, _8bit_bitshift_4_drop, _8bit_bitshift_5_drop, _8bit_bitshift_6_drop,
       _8bit_fa_1_ov, _8bit_fa_2_ov, A0, A1, A2, A3, and_22_out, B0, B1, B2, B3, Both_Neg, Neg, Not_Both_Neg,
       or_2_out, or_3_out, Ov_Change_A, Ov_Change_B, Ov_General, Ov_Sum_A, Ov_Sum_B;
  wire [3:0] A_inverted, A_Normal, A_not_change, A_t, A_t_t, B_inverted, B_Normal, B_not_change, B_t, B_t_t;
  wire [7:0] _8bit_bitshift_2_out, _8bit_bitshift_4_out, _8bit_bitshift_5_out, _8bit_fa_1_s, _8bit_fa_2_s,
       and_1_out, and_2_out, and_12_out, C0, C1, C2, C3;

  and and_1 (and_1_out[7], Neg, B1);
  and and_2 (and_2_out[7], Neg, B2);
  and and_3 (and_1_out[3], A3, B1);
  LED led_1 (.in(_8bit_bitshift_1_drop));
  _8bit_bitshift _8bit_bitshift_1 (.In({{4{and_1_out[7]}}, and_1_out[3:0]}), .Drop(_8bit_bitshift_1_drop), .Out(C1));
  and and_4 (and_1_out[2], A2, B1);
  and and_5 (and_2_out[3], A3, B2);
  and and_6 (and_1_out[1], A1, B1);
  and and_7 (and_2_out[2], A2, B2);
  and and_8 (and_1_out[0], A0, B1);
  and and_9 (and_2_out[1], A1, B2);
  _8bit_bitshift _8bit_bitshift_2 (
    .In({{4{and_2_out[7]}}, and_2_out[3:0]}), .Drop(_8bit_bitshift_2_drop), .Out(_8bit_bitshift_2_out));
  _8bit_bitshift _8bit_bitshift_3 (.In(_8bit_bitshift_2_out), .Drop(_8bit_bitshift_3_drop), .Out(C2));
  LED led_2 (.in(_8bit_bitshift_3_drop));
  and and_10 (and_2_out[0], A0, B2);
  LED led_3 (.in(_8bit_bitshift_2_drop));
  and and_11 (C0[0], A0, B0);
  and and_12 (and_12_out[0], A0, B3);
  and and_13 (C0[1], A1, B0);
  and and_14 (and_12_out[1], A1, B3);
  and and_15 (C0[2], A2, B0);
  and and_16 (and_12_out[2], A2, B3);
  and and_17 (C0[3], A3, B0);
  and and_18 (and_12_out[3], A3, B3);
  _8bit_bitshift _8bit_bitshift_4 (
    .In({{4{and_12_out[7]}}, and_12_out[3:0]}), .Drop(_8bit_bitshift_4_drop), .Out(_8bit_bitshift_4_out));
  _8bit_bitshift _8bit_bitshift_5 (.In(_8bit_bitshift_4_out), .Drop(_8bit_bitshift_5_drop), .Out(_8bit_bitshift_5_out));
  LED led_4 (.in(_8bit_bitshift_5_drop));
  _8bit_bitshift _8bit_bitshift_6 (.In(_8bit_bitshift_5_out), .Drop(_8bit_bitshift_6_drop), .Out(C3));
  LED led_5 (.in(_8bit_bitshift_6_drop));
  LED led_6 (.in(_8bit_bitshift_4_drop));
  and and_19 (C0[7], Neg, B0);
  and and_20 (and_12_out[7], Neg, B3);
  _8bit_Fa _8bit_fa_1 (.A({{4{C0[7]}}, C0[3:0]}), .B(C1), .Cin(1'b0), .Ov(_8bit_fa_1_ov), .S(_8bit_fa_1_s));
  xor xor_1 (Neg, B[3], A[3]);
  _8bit_Fa _8bit_fa_2 (.A(C2), .B(_8bit_fa_1_s), .Cin(_8bit_fa_1_ov), .Ov(_8bit_fa_2_ov), .S(_8bit_fa_2_s));
  _4bit___Checker _4bit___checker_1 (.Num(A), .Cin(Not_Both_Neg), .Out(A_Normal));
  _4bit___Checker _4bit___checker_2 (.Num(B), .Cin(Not_Both_Neg), .Out(B_Normal));
  _4_bit___opposite _4_bit___opposite_1 (.Num(A), .Cin(Both_Neg), .Output(A_t));
  _4_bit___opposite _4_bit___opposite_2 (.Num(B), .Cin(Both_Neg), .Output(B_t));
  _8bit_Fa _8bit_fa_3 (.A(C3), .B(_8bit_fa_2_s), .Cin(_8bit_fa_2_ov), .Ov(Ov_General), .S(Output));
  and and_21 (Both_Neg, B[3], A[3]);
  not not_1 (Not_Both_Neg, Both_Neg);
  _4bit_Fa _4bit_fa_1 (.A(A_Normal), .B(A_t), .Cin(1'b0), .S(A_t_t), .Ov(Ov_Sum_A));
  _4bit_Fa _4bit_fa_2 (.A(B_Normal), .B(B_t), .Cin(1'b0), .S(B_t_t), .Ov(Ov_Sum_B));
  _4_bit__Compair _4_bit__compair_1 (
    .A(A_t_t), .B(B_t_t), .eq(_4_bit__compair_1_eq), .gt(_4_bit__compair_1_gt), .lt(_4_bit__compair_1_lt));
  _4_bit__Compair _4_bit__compair_2 (
    .A(B_t_t), .B(A_t_t), .eq(_4_bit__compair_2_eq), .gt(_4_bit__compair_2_gt), .lt(_4_bit__compair_2_lt));
  or or_1 (Ov, Ov_Sum_A, Ov_Sum_B, Ov_Change_A, Ov_Change_B, Ov_General);
  or or_2 (or_2_out, _4_bit__compair_1_eq, _4_bit__compair_1_lt);
  or or_3 (or_3_out, _4_bit__compair_2_eq, _4_bit__compair_2_gt);
  and and_22 (and_22_out, _4_bit__compair_1_gt, _4_bit__compair_2_lt);
  _4bit___Checker _4bit___checker_3 (.Num(A_t_t), .Cin(or_2_out), .Out(A_not_change));
  _4bit___Checker _4bit___checker_4 (.Num(B_t_t), .Cin(or_3_out), .Out(B_not_change));
  _4bit___Checker _4bit___checker_5 (.Num(B_t_t), .Cin(and_22_out), .Out(A_inverted));
  _4bit___Checker _4bit___checker_6 (.Num(A_t_t), .Cin(and_22_out), .Out(B_inverted));
  _4bit_Fa _4bit_fa_3 (.A(A_not_change), .B(A_inverted), .Cin(1'b0), .S({A3, A2, A1, A0}), .Ov(Ov_Change_A));
  _4bit_Fa _4bit_fa_4 (.A(B_not_change), .B(B_inverted), .Cin(1'b0), .S({B3, B2, B1, B0}), .Ov(Ov_Change_B));

  // Other names for the same wires on the sheet: C0[6:4] = {3{C0[7]}}; A0_Raw = A[0]; A_Raw[3:0] = A; A1_Raw = A[1];
  //   A2_Raw = A[2]; A3_Raw = A[3]; B0_Raw = B[0]; B_Raw[3:0] = B; B1_Raw = B[1]; B2_Raw = B[2]; B3_Raw = B[3]
endmodule
