// Digital circuit 8bit-Compar.dig as structural Verilog
module _8bit_Compar (
  input  [7:0] A,
  input  [7:0] B,
  output eq,
  output gt,
  output lt
);

  wire _1__lt, _1_eq_1, _1_eq_2, _1_eq_3, _1_eq_4, _1_eq_5, _1_eq_6, _1_eq_7, _1bit_compar_1_gt,
       _1bit_compar_1_lt, _1bit_compar_2_gt, _1bit_compar_2_lt, _1bit_compar_3_gt, _1bit_compar_3_lt,
       _1bit_compar_4_gt, _1bit_compar_5_gt, _1bit_compar_5_lt, _1bit_compar_6_gt, _1bit_compar_6_lt,
       _1bit_compar_7_gt, _1bit_compar_7_lt, _1bit_compar_8_gt, _1bit_compar_8_lt;

  _1bit_Compar _1bit_compar_1 (
    ._1_eq(1'b1), .A(A[7]), .B(B[7]), .eq(_1_eq_7), .gt(_1bit_compar_1_gt), .lt(_1bit_compar_1_lt));
  _1bit_Compar _1bit_compar_2 (
    ._1_eq(_1_eq_7), .A(A[6]), .B(B[6]), .eq(_1_eq_6), .gt(_1bit_compar_2_gt), .lt(_1bit_compar_2_lt));
  _1bit_Compar _1bit_compar_3 (
    ._1_eq(_1_eq_6), .A(A[5]), .B(B[5]), .eq(_1_eq_5), .gt(_1bit_compar_3_gt), .lt(_1bit_compar_3_lt));
  _1bit_Compar _1bit_compar_4 (._1_eq(_1_eq_5), .A(A[4]), .B(B[4]), .eq(_1_eq_4), .gt(_1bit_compar_4_gt), .lt(_1__lt));
  _1bit_Compar _1bit_compar_5 (
    ._1_eq(_1_eq_4), .A(A[3]), .B(B[3]), .eq(_1_eq_3), .gt(_1bit_compar_5_gt), .lt(_1bit_compar_5_lt));
  xor xor_1 (gt, _1bit_compar_8_gt, _1bit_compar_7_gt, _1bit_compar_6_gt, _1bit_compar_5_gt, _1bit_compar_4_gt, _1bit_compar_3_gt, _1bit_compar_2_gt, _1bit_compar_1_lt);
  _1bit_Compar _1bit_compar_6 (
    ._1_eq(_1_eq_3), .A(A[2]), .B(B[2]), .eq(_1_eq_2), .gt(_1bit_compar_6_gt), .lt(_1bit_compar_6_lt));
  _1bit_Compar _1bit_compar_7 (
    ._1_eq(_1_eq_2), .A(A[1]), .B(B[1]), .eq(_1_eq_1), .gt(_1bit_compar_7_gt), .lt(_1bit_compar_7_lt));
  _1bit_Compar _1bit_compar_8 (
    ._1_eq(_1_eq_1), .A(A[0]), .B(B[0]), .eq(eq), .gt(_1bit_compar_8_gt), .lt(_1bit_compar_8_lt));
  xor xor_2 (lt, _1bit_compar_8_lt, _1bit_compar_7_lt, _1bit_compar_6_lt, _1bit_compar_5_lt, _1__lt, _1bit_compar_3_lt, _1bit_compar_2_lt, _1bit_compar_1_gt);
endmodule
