// Digital circuit 8bit-Fa.dig as structural Verilog
module _8bit_Fa (
  input  [7:0] A,
  input  [7:0] B,
  input  Cin,
  output Ov,
  output [7:0] S
);

  wire fa_1_cout, fa_2_cout, fa_3_cout, fa_4_cout, fa_5_cout, fa_6_cout, fa_7_cout, fa_8_cout;

  Fa fa_1 (.A(A[0]), .B(B[0]), .Cin(Cin), .S(S[0]), .Cout(fa_1_cout));
  Fa fa_2 (.A(A[1]), .B(B[1]), .Cin(fa_1_cout), .S(S[1]), .Cout(fa_2_cout));
  Fa fa_3 (.A(A[2]), .B(B[2]), .Cin(fa_2_cout), .S(S[2]), .Cout(fa_3_cout));
  Fa fa_4 (.A(A[3]), .B(B[3]), .Cin(fa_3_cout), .S(S[3]), .Cout(fa_4_cout));
  Fa fa_5 (.A(A[4]), .B(B[4]), .Cin(fa_4_cout), .S(S[4]), .Cout(fa_5_cout));
  Fa fa_6 (.A(A[5]), .B(B[5]), .Cin(fa_5_cout), .S(S[5]), .Cout(fa_6_cout));
  Fa fa_7 (.A(A[6]), .B(B[6]), .Cin(fa_6_cout), .S(S[6]), .Cout(fa_7_cout));
  Fa fa_8 (.A(A[7]), .B(B[7]), .Cin(fa_7_cout), .S(S[7]), .Cout(fa_8_cout));
  xor xor_1 (Ov, fa_8_cout, fa_7_cout);
endmodule
