// Digital circuit 8bit-Fs.dig as structural Verilog
module _8bit_Fs (
  input  [7:0] A,
  input  [7:0] B,
  output [7:0] S,
  output Ov
);

  wire [7:0] not_1_out;

  assign not_1_out = ~B;  // Not not_1, 8 bits wide
  _8bit_Fa _8bit_fa_1 (.A(A), .B(not_1_out), .Cin(1'b1), .Ov(Ov), .S(S));
endmodule
