// Digital circuit 8bit-Multiplier.dig as structural Verilog
module _8bit_Multiplier (
  input  [3:0] B,
  input  [3:0] A,
  output [7:0] Output,
  output Ov
);

  wire _8bit_bitshift_1_drop, _8bit_bitshift_2_drop, _8bit_bitshift_3_drop, _8bit_bitshift_4_drop,
       _8bit_bitshift_5_drop, _8bit_bitshift_6_drop, _8bit_fa_1_ov, _8bit_fa_2_ov;
  wire [3:0] and_6_out, and_8_out, and_16_out, C0;
  wire [7:0] _8bit_bitshift_2_out, _8bit_bitshift_4_out, _8bit_bitshift_5_out, _8bit_fa_1_s, _8bit_fa_2_s,
       C1, C2, C3;

  and and_1 (and_6_out[3], A[3], B[1]);
  LED led_1 (.in(_8bit_bitshift_1_drop));
  _8bit_bitshift _8bit_bitshift_1 (.In({4'b0000, and_6_out}), .Drop(_8bit_bitshift_1_drop), .Out(C1));
  and and_2 (and_6_out[2], A[2], B[1]);
  and and_3 (and_8_out[3], A[3], B[2]);
  and and_4 (and_6_out[1], A[1], B[1]);
  and and_5 (and_8_out[2], A[2], B[2]);
  and and_6 (and_6_out[0], A[0], B[1]);
  and and_7 (and_8_out[1], A[1], B[2]);
  _8bit_bitshift _8bit_bitshift_2 (.In({4'b0000, and_8_out}), .Drop(_8bit_bitshift_2_drop), .Out(_8bit_bitshift_2_out));
  _8bit_bitshift _8bit_bitshift_3 (.In(_8bit_bitshift_2_out), .Drop(_8bit_bitshift_3_drop), .Out(C2));
  LED led_2 (.in(_8bit_bitshift_3_drop));
  and and_8 (and_8_out[0], A[0], B[2]);
  LED led_3 (.in(_8bit_bitshift_2_drop));
  and and_9 (C0[0], A[0], B[0]);
  and and_10 (and_16_out[0], A[0], B[3]);
  and and_11 (C0[1], A[1], B[0]);
  and and_12 (and_16_out[1], A[1], B[3]);
  and and_13 (C0[2], A[2], B[0]);
  and and_14 (and_16_out[2], A[2], B[3]);
  and and_15 (C0[3], A[3], B[0]);
  and and_16 (and_16_out[3], A[3], B[3]);
  _8bit_bitshift _8bit_bitshift_4 (
    .In({4'b0000, and_16_out}), .Drop(_8bit_bitshift_4_drop), .Out(_8bit_bitshift_4_out));
  _8bit_bitshift _8bit_bitshift_5 (.In(_8bit_bitshift_4_out), .Drop(_8bit_bitshift_5_drop), .Out(_8bit_bitshift_5_out));
  LED led_4 (.in(_8bit_bitshift_5_drop));
  _8bit_bitshift _8bit_bitshift_6 (.In(_8bit_bitshift_5_out), .Drop(_8bit_bitshift_6_drop), .Out(C3));
  LED led_5 (.in(_8bit_bitshift_6_drop));
  LED led_6 (.in(_8bit_bitshift_4_drop));
  _8bit_Fa _8bit_fa_1 (.A({4'b0000, C0}), .B(C1), .Cin(1'b0), .Ov(_8bit_fa_1_ov), .S(_8bit_fa_1_s));
  _8bit_Fa _8bit_fa_2 (.A(C2), .B(_8bit_fa_1_s), .Cin(_8bit_fa_1_ov), .Ov(_8bit_fa_2_ov), .S(_8bit_fa_2_s));
  _8bit_Fa _8bit_fa_3 (.A(C3), .B(_8bit_fa_2_s), .Cin(_8bit_fa_2_ov), .Ov(Ov), .S(Output));
endmodule
