// Digital circuit 8bit-bitshift.dig as structural Verilog
module _8bit_bitshift (
  input  [7:0] In,
  output Drop,
  output [7:0] Out
);


  assign Drop = In[7];
  assign Out = {In[6:0], 1'b0};
endmodule
