// Digital circuit Teste-4bit-Fa.dig as structural Verilog
module Teste_4bit_Fa (
  input  [3:0] in_1,
  input  [3:0] in_2
);

  wire _4bit_fa_1_ov;
  wire [3:0] _4bit_fa_1_s;

  _4bit_Fa _4bit_fa_1 (.A(in_1), .B(in_2), .S(_4bit_fa_1_s), .Ov(_4bit_fa_1_ov));  // open: Cin
  Seven_Seg_Hex seven_seg_hex_1 (.d(_4bit_fa_1_s), .dp(1'b0));
  LED led_1 (.in(_4bit_fa_1_ov));
endmodule
