// Digital circuit Using 8 bit ALU.dig as structural Verilog
module Using_8_bit_ALU (
  input  [7:0] A,
  input  [7:0] B,
  input  [2:0] Opcode,
  output Ov,
  output A__eq__B,
  output A__gt__B,
  output A__lt__B,
  output [7:0] S
);

  wire [3:0] bits_0_3, bits_4_7;
  wire [7:0] _8_bit___oppposite_raw_1_output;

  Seven_Seg seven_seg_1 (.a(1'b0), .b(1'b0), .c(1'b0), .d(1'b0), .e(1'b0), .f(1'b0), .g(S[7]), .dp(1'b0));
  Seven_Seg_Hex seven_seg_hex_1 (.d(bits_4_7), .dp(1'b0));
  Seven_Seg_Hex seven_seg_hex_2 (.d(bits_0_3), .dp(1'b0));
  _8_bit_ALU _8_bit_alu_1 (.A(A), .B(B), .Opcode(Opcode), .S(S), .Ov(Ov), .eq(A__eq__B), .gt(A__gt__B), .lt(A__lt__B));
  _8_bit___oppposite_raw _8_bit___oppposite_raw_1 (.Num(S), .Output(_8_bit___oppposite_raw_1_output));
  Multiplexer #(.Bits(8)) multiplexer_1 (
    .sel(S[7]), .in_0(S), .in_1(_8_bit___oppposite_raw_1_output), .out({bits_4_7, bits_0_3}));

  // Other names for the same wires on the sheet: Signal = S[7]
endmodule
